# Fritzing sketch Atmega32LBrokeOut-updated (saved by Fritzing 0.9.2b)
breadboards: 4

parts:
  Atmel's_Atmega32L_Microchip1 = AVR-Atmega32 [package="DIP (Dual Inline)"]
  R1 = Resistor [resistance=10k tolerance=±5% package=THT]
  S1 = Pushbutton [package="[THT]"]
  R2 = Resistor [resistance=220 tolerance=±5% package=THT]
  XTAL1 = Crystal [frequency="16 Mhz" package=THT]
  LED3 = LED - 5mm [color="Green (555nm)" package="5 mm [THT]"]
  LED1 = LED - 5mm [color="Blue (430nm)" package="5 mm [THT]"]
  LED2 = LED - 5mm [color="Red (633nm)" package="5 mm [THT]"]
  Arduino1 = Arduino Uno (Rev3)

nets:
  N1: Atmel's_Atmega32L_Microchip1.pin_9, R1.Pin_0
  N2: Atmel's_Atmega32L_Microchip1.pin_10, Atmel's_Atmega32L_Microchip1.pin_30, R1.Pin_1, S1.Pin_2
  N3: Atmel's_Atmega32L_Microchip1.pin_11, Atmel's_Atmega32L_Microchip1.pin_31, S1.Pin_4, Arduino1.GND
  N4: Atmel's_Atmega32L_Microchip1.pin_12, XTAL1.pin_1
  N5: Atmel's_Atmega32L_Microchip1.pin_13, XTAL1.pin_0
  N6: R2.Pin_1, LED3.cathode, LED1.cathode, LED2.cathode
  N7: LED3.anode, Arduino1.D7
  N8: LED2.anode, Arduino1.D8

notes:
  RX/TX Lines / Multipurpose I/O
  AHREF
  Reset
  16mhz Oscillator
  ADC Mutipurpose I/O
  Bi-Directional I/O + JTAG Function Lines
  Multipurpose I/O
  ICSP Programming Lines
  Programming leds:
  Blue: ICSP Heartbeat
  Red: Programming
  Error
  Green: Programming in
  progress

custom parts:
  AVR-Atmega32: Atmel's Atmega32. A beast of an 8 bit microchip to behold! This is not your dad's arduino chip! Also the DIP version of the microchip that is at the helm of the Arduino Mega. For more info, consult the datasheet: http://www.atmel.com/dyn/resources/prod_documents/doc2503.pdf
