# Fritzing sketch Sketch3 (saved by Fritzing 0.9.2b)
breadboards: 2

parts:
  Y1 = CRYSTAL [package=crystal-32khz-smd]
  U3 = PIC-ICSP [package=molex-1x6]
  Atmel's_Atmega32L_Microchip1 = AVR-Atmega32 [package="DIP (Dual Inline)"]
  C1 = Tantalum Capacitor [capacitance=1μF package="100 mil [THT, tantalum]"]
  Q1 = Basic FET P-Channel [package="TO220 [THT]"]
  VCC1 = Battery block 9V
  Matrix_keypad2 = KEYPAD 4x4
  U4 = LCD-16X2 [package=lcd-16x2_noholes]
  R1 = Resistor [tolerance=±5% resistance=220 package="0402 [SMD]"]
  C2 = Tantalum Capacitor [capacitance=1μF package="100 mil [THT, tantalum]"]
  C3 = Tantalum Capacitor [capacitance=1μF package="100 mil [THT, tantalum]"]
  C4 = Tantalum Capacitor [capacitance=1μF package="100 mil [THT, tantalum]"]
  J1 = Piezo Speaker

nets:
  N1: Y1.1, Atmel's_Atmega32L_Microchip1.pin_12
  N2: Y1.2, Atmel's_Atmega32L_Microchip1.pin_13
  N3: U3.PGM, Atmel's_Atmega32L_Microchip1.pin_7
  N4: U3.PGC, Atmel's_Atmega32L_Microchip1.pin_8
  N5: U3.PGD, Atmel's_Atmega32L_Microchip1.pin_9
  N6: U3.GND, Atmel's_Atmega32L_Microchip1.pin_10, Atmel's_Atmega32L_Microchip1.pin_30, Q1.source, U4.RS
  N7: U3.VCC, Atmel's_Atmega32L_Microchip1.pin_6
  N8: U3.VPP, Atmel's_Atmega32L_Microchip1.pin_11, Atmel's_Atmega32L_Microchip1.pin_31, C1.-, Q1.drain, VCC1.-, U4.VO, R1.Pin_1, J1.pin1
  N9: Atmel's_Atmega32L_Microchip1.pin_1, U4.E
  N10: Atmel's_Atmega32L_Microchip1.pin_2, U4.DB0
  N11: Atmel's_Atmega32L_Microchip1.pin_3, U4.DB1
  N12: Atmel's_Atmega32L_Microchip1.pin_14, U4.DB2
  N13: Atmel's_Atmega32L_Microchip1.pin_15, U4.DB3
  N14: Atmel's_Atmega32L_Microchip1.pin_16, U4.DB4
  N15: Atmel's_Atmega32L_Microchip1.pin_17, U4.DB5
  N16: Atmel's_Atmega32L_Microchip1.pin_18, U4.DB6
  N17: Atmel's_Atmega32L_Microchip1.pin_19, U4.DB7
  N18: Atmel's_Atmega32L_Microchip1.pin_20, U4.A
  N19: Atmel's_Atmega32L_Microchip1.pin_21, U4.K
  N20: Atmel's_Atmega32L_Microchip1.pin_22, Matrix_keypad2.row4
  N21: Atmel's_Atmega32L_Microchip1.pin_23, Matrix_keypad2.row3
  N22: Atmel's_Atmega32L_Microchip1.pin_24, Matrix_keypad2.row2
  N23: Atmel's_Atmega32L_Microchip1.pin_25, Matrix_keypad2.row1
  N24: Atmel's_Atmega32L_Microchip1.pin_26, Matrix_keypad2.col4
  N25: Atmel's_Atmega32L_Microchip1.pin_27, Matrix_keypad2.col3
  N26: Atmel's_Atmega32L_Microchip1.pin_28, Matrix_keypad2.col2
  N27: Atmel's_Atmega32L_Microchip1.pin_29, Matrix_keypad2.col1
  N28: Atmel's_Atmega32L_Microchip1.pin_37, C4.+
  N29: Atmel's_Atmega32L_Microchip1.pin_38, C3.+
  N30: Atmel's_Atmega32L_Microchip1.pin_40, C2.+
  N31: C1.+, Q1.gate, VCC1.+
  N32: U4.R_W, R1.Pin_0
  N33: C2.-, C3.-, C4.-, J1.pin2

custom parts:
  AVR-Atmega32: Atmel's Atmega32. A beast of an 8 bit microchip to behold! This is not your dad's arduino chip! Also the DIP version of the microchip that is at the helm of the Arduino Mega. For more info, consult the datasheet: http://www.atmel.com/dyn/resources/prod_documents/doc2503.pdf
  KEYPAD 4x4: Matrix keypad 16 buttons, 4 rows x 4 columns
